# Fritzing sketch led2 (saved by Fritzing 0.9.1b)
breadboards: 1

parts:
  Raspberry_Pi1 = Raspberry Pi B+
  LED1 = LED - 5mm [color="Red (633nm)" package="5 mm [THT]"]
  R1 = Resistor [tolerance=±5% resistance=330 package=THT]

nets:
  N1: Raspberry_Pi1.GND, LED1.cathode
  N2: Raspberry_Pi1.GPIO25, R1.Pin_0
  N3: LED1.anode, R1.Pin_1
