# Fritzing sketch tact-led (saved by Fritzing 0.9.1b)
breadboards: 1

parts:
  Raspberry_Pi1 = Raspberry Pi B+
  LED1 = LED - 5mm [color="Red (633nm)" package="5 mm [THT]"]
  R1 = Resistor [tolerance=±5% resistance=330 package=THT]
  S1 = Pushbutton [package="[THT]"]

nets:
  3V3: Raspberry_Pi1.3v3, Raspberry_Pi1.3V3, S1.Pin_3, S1.Pin_4
  N1: Raspberry_Pi1.GND, LED1.cathode
  N2: Raspberry_Pi1.GPIO25, R1.Pin_0
  N3: Raspberry_Pi1.GPIO24, S1.Pin_1, S1.Pin_2
  N4: LED1.anode, R1.Pin_1
