# Fritzing sketch tact-pulldown (saved by Fritzing 0.9.1b)
breadboards: 1

parts:
  Raspberry_Pi1 = Raspberry Pi B+
  S1 = Pushbutton [package="[THT]"]

nets:
  3V3: Raspberry_Pi1.3v3, Raspberry_Pi1.3V3, S1.Pin_3, S1.Pin_4
  N1: Raspberry_Pi1.GPIO24, S1.Pin_1, S1.Pin_2
